# Fritzing sketch Placa PhysioMetrics_v3 (saved by Fritzing 0.9.3b)
circuit board: 5.32757cm x 4.97102cm
perfboards: 1

parts:
  Arduino_Nano = Arduino Nano (Rev3.0)
  BT = female pin header, 6 pins [form="♀ (female)"]
  HR = female pin header, 4 pins [form="♀ (female)"]
  GSR = female pin header, 4 pins [form="♀ (female)"]
  EMG = female pin header, 4 pins [form="♀ (female)"]
  R2 = Resistor [tolerance=±5% resistance=220 package=THT]
  R3 = Resistor [tolerance=±5% resistance=270 package=THT]

nets:
  N1: Arduino_Nano.GND, BT.pin4, HR.pin4, GSR.pin4, EMG.pin4, R3.Pin_1
  N2: Arduino_Nano.D2, R2.Pin_0
  N3: Arduino_Nano.D3, BT.pin2
  N4: Arduino_Nano.D4, HR.pin1
  N5: Arduino_Nano.5V, BT.pin5
  N6: Arduino_Nano.A1, GSR.pin1
  N7: Arduino_Nano.A0, EMG.pin1
  N8: Arduino_Nano.3V3, HR.pin3, GSR.pin3, EMG.pin3
  N9: BT.pin3, R2.Pin_1, R3.Pin_0

notes:
  physio(m)etrics
